// Logisim project Projectviva.circ as structural Verilog: 1 circuit, main circuit main
module main (
  input  A,
  input  B,
  input  C
);

  wire nor_1_out, nor_2_out, nor_3_out, nor_4_out, nor_5_out, nor_6_out, nor_7_out, nor_8_out, nor_9_out,
       nor_10_out, nor_11_out, nor_12_out, nor_13_out, nor_14_out, nor_15_out, nor_16_out, nor_17_out,
       nor_18_out, nor_19_out, nor_20_out, nor_21_out, nor_22_out, nor_23_out, nor_24_out, nor_25_out;

  nor nor_1 (nor_1_out, A, A);
  nor nor_2 (nor_2_out, B, B);
  nor nor_3 (nor_3_out, C, C);
  nor nor_4 (nor_4_out, A, B);
  nor nor_5 (nor_5_out, nor_1_out, nor_2_out);
  nor nor_6 (nor_6_out, A, B);
  nor nor_7 (nor_7_out, A, B);
  nor nor_8 (nor_8_out, nor_1_out, nor_2_out);
  nor nor_9 (nor_9_out, B, A);
  nor nor_10 (nor_10_out, B, nor_3_out);
  nor nor_11 (nor_11_out, nor_1_out, nor_2_out);
  nor nor_12 (nor_12_out, A, nor_3_out);
  nor nor_13 (nor_13_out, nor_4_out, nor_3_out);
  nor nor_14 (nor_14_out, nor_13_out, nor_13_out);
  nor nor_15 (nor_15_out, nor_5_out, nor_5_out);
  nor nor_16 (nor_16_out, nor_6_out, nor_6_out);
  nor nor_17 (nor_17_out, nor_16_out, C);
  nor nor_18 (nor_18_out, nor_3_out, nor_7_out);
  nor nor_19 (nor_19_out, nor_18_out, nor_18_out);
  nor nor_20 (nor_20_out, nor_8_out, nor_9_out);
  nor nor_21 (nor_21_out, nor_20_out, nor_20_out);
  nor nor_22 (nor_22_out, nor_10_out, nor_11_out);
  nor nor_23 (nor_23_out, nor_12_out, nor_12_out);
  nor nor_24 (nor_24_out, nor_17_out, nor_17_out);
  nor nor_25 (nor_25_out, nor_22_out, nor_22_out);
  _7_Segment_Display u_7_segment_display_1 (
    .g(nor_23_out), .f(nor_25_out), .a(nor_14_out), .b(nor_15_out), .e(nor_21_out), .d(nor_19_out),
    .c(nor_24_out));  // open: dp

  // Notes on the sheet:
  //                                       NAME: BUSHRA HOSSAIN
  //           b=A'+B'
  //                                        g=A+C'
  //             a=C'+A'B'
  //                 c=C+A+B
  //               d=C'+A'B'
  //                          e=AB+A'B'
  //          f=B'C+AB
  //                                                          NSU ID : 203 1346 642
endmodule
